# Fritzing sketch colormixer (saved by Fritzing 0.9.2b)
breadboards: 1

parts:
  Part1 = Arduino Pro Mini v13
  Power_plug1 = Power plug
  C1 = Electrolytic Capacitor [capacitance=0.1mF package="100 mil [THT, electrolytic]"]
  U1 = POT [package=alps_pot]
  U2 = POT [package=alps_pot]
  U3 = POT [package=alps_pot]
  LED1 = RGB LED (com. anode, rbg) [package="5 mm [THT]"]
  NEOPIXEL1 = Neopixel Strip -- White (30/m)
  R1 = Resistor [tolerance=±5% resistance=220 package=THT]
  R2 = Resistor [tolerance=±5% resistance=220 package=THT]
  R3 = Resistor [tolerance=±5% resistance=220 package=THT]
  R4 = Resistor [tolerance=±5% resistance=330 package=THT]

nets:
  VCC: Part1.RAW, Power_plug1.VCC, C1.+, U1.E, U1.A, U2.E, U2.A, U3.E, U3.A, LED1.common_anode, NEOPIXEL1.+5V
  GND: Part1.GND, Power_plug1.GND, C1.-, NEOPIXEL1.GND
  N1: Part1.A3, U3.S
  N2: Part1.A2, U2.S
  N3: Part1.A1, U1.S
  N4: Part1.D11_PWM/MOSI, R3.Pin_0
  N5: Part1.D10_PWM/SS, R1.Pin_0
  N6: Part1.D9_PWM, Part1.D8, R2.Pin_0
  N7: Part1.D4, R4.Pin_0
  N8: LED1.red_cathode, R2.Pin_1
  N9: LED1.blue_cathode, R1.Pin_1
  N10: LED1.green_cathode, R3.Pin_1
  N11: NEOPIXEL1.Din, R4.Pin_1

custom parts:
  Neopixel Strip -- White (30/m): These NeoPixel strips have 30 digitally-addressable pixel LEDs per meter and are very affordable and are only 12.5 mm wide, 10 mm if you remove the strip from the casing.
